// Logisim project Matheus Endlich Silveira- MCU_4bits_CC3MB_24.circ as structural Verilog: 16 circuits, main circuit Main 👽
module Main (
);

  wire alu_1_overflow, alu_1_zero, clock_1_out, d_ff_1_q, d_ff_2_q, not_1_out, not_2_out, Reset_out,
       unidade_de_controle_1_clk_ag, unidade_de_controle_1_clk_pc, unidade_de_controle_1_clk_ram,
       unidade_de_controle_1_clk_rl, \unidade_de_controle_1_direção , unidade_de_controle_1_e,
       unidade_de_controle_1_load, unidade_de_controle_1_r_w, unidade_de_controle_1_rst_pc;
  wire [2:0] \unidade_de_controle_1_operação ;
  wire [3:0] ac_1_q, alu_1_saida, counter_1_q, mux_1_s, ram_1_data, \unidade_de_controle_1_b_endereços ,
       unidade_de_controle_1_dados, unidade_de_controle_1_operando;
  wire [7:0] ir_1_q, rom_1_data;

  Counter #(.width(4), .max('hf), .trigger("falling")) counter_1 (
    .load(unidade_de_controle_1_load), .D(unidade_de_controle_1_dados), .count(not_1_out), .Q(counter_1_q),
    .clk(unidade_de_controle_1_clk_pc), .clr(unidade_de_controle_1_rst_pc));  // open: carry
  not not_1 (not_1_out, unidade_de_controle_1_load);
  Clock clock_1 (.out(clock_1_out));
  ROM #(.addrWidth(4)) rom_1 (.addr(counter_1_q), .data(rom_1_data));  // open: sel
  IR ir_1 (.Clock(unidade_de_controle_1_clk_rl), .Q(ir_1_q), .D(rom_1_data));
  // Probe on ir_1_q
  Unidade_de_Controle unidade_de_controle_1 (
    .\B_Endereços (\unidade_de_controle_1_b_endereços ), .Operando(unidade_de_controle_1_operando),
    .\Direção (\unidade_de_controle_1_direção ), .E(unidade_de_controle_1_e),
    .\Operação (\unidade_de_controle_1_operação ), .\Instrução (ir_1_q), .Clock(clock_1_out),
    .Reset(Reset_out), .Rst_Pc(unidade_de_controle_1_rst_pc), .clk_Rl(unidade_de_controle_1_clk_rl),
    .clk_PC(unidade_de_controle_1_clk_pc), .clk_AG(unidade_de_controle_1_clk_ag),
    .clk_Ram(unidade_de_controle_1_clk_ram), .Dados(unidade_de_controle_1_dados), .OverFlow(d_ff_2_q),
    .Zero(d_ff_1_q), .Load(unidade_de_controle_1_load), .r_w(unidade_de_controle_1_r_w));
  Button Reset (.out(Reset_out));
  // Probe on ac_1_q
  ALU alu_1 (
    .\Direção (\unidade_de_controle_1_direção ), .A(ac_1_q), .B(mux_1_s),
    .\Operações (\unidade_de_controle_1_operação ), .Saida(alu_1_saida), .Overflow(alu_1_overflow),
    .Zero(alu_1_zero));
  AC ac_1 (.D(alu_1_saida), .Clock(unidade_de_controle_1_clk_ag), .Q(ac_1_q));
  Mux mux_1 (.E(unidade_de_controle_1_operando), .Controle(unidade_de_controle_1_e), .D(ram_1_data), .S(mux_1_s));
  // Probe on mux_1_s
  D_Flip_Flop d_ff_1 (
    .clk(unidade_de_controle_1_clk_ag), .D(alu_1_overflow), .Q(d_ff_1_q));  // open: Qn, preset, en, reset
  D_Flip_Flop d_ff_2 (.clk(unidade_de_controle_1_clk_ag), .D(alu_1_zero), .Q(d_ff_2_q));  // open: Qn, preset, en, reset
  // Probe on ac_1_q
  RAM #(.addrWidth(4), .dataWidth(4)) ram_1 (
    .addr(\unidade_de_controle_1_b_endereços ), .data(ram_1_data), .clk(unidade_de_controle_1_clk_ram),
    .ld(unidade_de_controle_1_r_w));  // open: sel, clr
  not not_2 (not_2_out, unidade_de_controle_1_r_w);
  Buffer buffer_1 (.B(ac_1_q), .in_2(not_2_out), .Saida(ram_1_data));

  // Notes on the sheet:
  //   MOV
  //   0
  //   1
  //   MOV
  //   2
  //   ADD
  //   3
  //   ADD
  //   SUB
  //   4
  //   5
  //   SUB
  //   6
  //   OR
  //   OR
  //   7
  //   8
  //   NOT
  //   NOT
  //   9
  //   SHF
  //   A
  //   B
  //   SHF
  //   JPZ
  //   C
  //   JPO
  //   D
  //   GO
  //   E
  //   STR
  //   F
  //   Instruction Set
  //   0
  //   000
  //   AC <= X
  //   1
  //   000
  //   AC <= M(X)
  //   0
  //   001
  //   1
  //   001
  //   010
  //   0
  //   AC <= AC-X
  //   1
  //   010
  //   0
  //   011
  //   1
  //   011
  //   0
  //   100
  //   100
  //   1
  //   101
  //   0
  //   1
  //   101
  //   0
  //   110
  //   110
  //   1
  //   PC <= X
  //   111
  //   0
  //   1
  //   M(X) <= AC 
  //   111
  //   AC <= AC+X
  //   AC <= AC+M(X)
  //   AC <= AC-M(X)
  //   AC <= AC OR X
  //   AC <= AC OR M(X)
  //   AC <= NOT X
  //   AC <= NOT M( X)
  //   AC <= AC << Q
  //   AC <= AC >> Q
  //   PC <= X SE FLAG Z
  //   PC <= X SE FLAG O
  //   PC 🤼‍
  //   contents of rom_1 (hex, n*v repeats v):
  //   0 f0 1 f1 10 31 d0 f2 11 f0 12 f1 e4
  //   Ovflw 😝
  //   Zero🤧
endmodule

module Add_1 (
  input  A,
  input  B,
  input  Vem_1,
  output Saida,
  output Vai_1
);

  wire and_1_out, and_2_out, or_1_out, xor_1_out;

  xor xor_1 (xor_1_out, A, B);
  or or_1 (or_1_out, B, Vem_1);
  xor xor_2 (Saida, xor_1_out, Vem_1);
  and and_1 (and_1_out, or_1_out, A);
  and and_2 (and_2_out, B, Vem_1);
  or or_2 (Vai_1, and_1_out, and_2_out);
endmodule

module Add_4 (
  input  [3:0] in_1,
  input  [3:0] in_2,
  input  Vem__1,
  output Vem_1,
  output [3:0] out_5
);

  wire add_1_2_vai_1, add_1_3_vai_1, add_1_4_vai_1;

  Add_1 add_1_1 (.A(in_2[3]), .B(in_1[3]), .Vem_1(add_1_2_vai_1), .Saida(out_5[3]), .Vai_1(Vem_1));
  Add_1 add_1_2 (.A(in_2[2]), .B(in_1[2]), .Vem_1(add_1_3_vai_1), .Saida(out_5[2]), .Vai_1(add_1_2_vai_1));
  Add_1 add_1_3 (.A(in_2[1]), .B(in_1[1]), .Vem_1(add_1_4_vai_1), .Saida(out_5[1]), .Vai_1(add_1_3_vai_1));
  Add_1 add_1_4 (.A(in_2[0]), .B(in_1[0]), .Vem_1(Vem__1), .Saida(out_5[0]), .Vai_1(add_1_4_vai_1));
endmodule

module Sub_1 (
  input  A,
  input  B,
  input  Vem_1,
  output Saida,
  output Vai_1
);

  wire and_1_out, and_2_out, not_1_out, or_1_out, xor_1_out;

  not not_1 (not_1_out, A);
  xor xor_1 (xor_1_out, A, B);
  or or_1 (or_1_out, B, Vem_1);
  xor xor_2 (Saida, xor_1_out, Vem_1);
  and and_1 (and_1_out, or_1_out, not_1_out);
  and and_2 (and_2_out, B, Vem_1);
  or or_2 (Vai_1, and_1_out, and_2_out);
endmodule

module Sub_4 (
  input  [3:0] B,
  input  [3:0] A,
  input  Vem_1,
  output Overflow,
  output [3:0] out_5
);

  wire sub_1_2_vai_1, sub_1_3_vai_1, sub_1_4_vai_1;

  Sub_1 sub_1_1 (.A(A[3]), .B(B[3]), .Vem_1(sub_1_2_vai_1), .Saida(out_5[3]), .Vai_1(Overflow));
  Sub_1 sub_1_2 (.A(A[2]), .B(B[2]), .Vem_1(sub_1_3_vai_1), .Saida(out_5[2]), .Vai_1(sub_1_2_vai_1));
  Sub_1 sub_1_3 (.A(A[1]), .B(B[1]), .Vem_1(sub_1_4_vai_1), .Saida(out_5[1]), .Vai_1(sub_1_3_vai_1));
  Sub_1 sub_1_4 (.A(A[0]), .B(B[0]), .Vem_1(Vem_1), .Saida(out_5[0]), .Vai_1(sub_1_4_vai_1));
endmodule

module Buffer (
  input  [3:0] B,
  input  in_2,
  output [3:0] Saida
);

  assign Saida[3] = in_2 ? B[3] : 1'bz;  // Controlled_Buffer controlled_buffer_1
  assign Saida[2] = in_2 ? B[2] : 1'bz;  // Controlled_Buffer controlled_buffer_2
  assign Saida[1] = in_2 ? B[1] : 1'bz;  // Controlled_Buffer controlled_buffer_3
  assign Saida[0] = in_2 ? B[0] : 1'bz;  // Controlled_Buffer controlled_buffer_4
endmodule

module Buffer_N (
  input  [3:0] B,
  input  in_2,
  output [3:0] Saida
);

  assign Saida[3] = in_2 ? ~B[3] : 1'bz;  // Controlled_Inverter controlled_inverter_1
  assign Saida[2] = in_2 ? ~B[2] : 1'bz;  // Controlled_Inverter controlled_inverter_2
  assign Saida[1] = in_2 ? ~B[1] : 1'bz;  // Controlled_Inverter controlled_inverter_3
  assign Saida[0] = in_2 ? ~B[0] : 1'bz;  // Controlled_Inverter controlled_inverter_4
endmodule

module Decoder (
  input  [2:0] A_B_C,
  output S0,
  output S1,
  output S2,
  output S3,
  output S4,
  output S5,
  output S6,
  output S7
);

  wire not_1_out, not_2_out, not_3_out, not_4_out, not_5_out, not_6_out, not_7_out, not_8_out, not_9_out,
       not_10_out, not_11_out, not_12_out;

  not not_1 (not_1_out, A_B_C[2]);
  not not_2 (not_2_out, A_B_C[1]);
  not not_3 (not_3_out, A_B_C[0]);
  not not_4 (not_4_out, A_B_C[2]);
  not not_5 (not_5_out, A_B_C[1]);
  not not_6 (not_6_out, A_B_C[2]);
  not not_7 (not_7_out, A_B_C[0]);
  not not_8 (not_8_out, A_B_C[2]);
  not not_9 (not_9_out, A_B_C[1]);
  not not_10 (not_10_out, A_B_C[0]);
  not not_11 (not_11_out, A_B_C[1]);
  not not_12 (not_12_out, A_B_C[0]);
  and and_1 (S7, A_B_C[2], A_B_C[1], A_B_C[0]);
  and and_2 (S0, not_1_out, not_2_out, not_3_out);
  and and_3 (S1, not_4_out, not_5_out, A_B_C[0]);
  and and_4 (S2, not_6_out, A_B_C[1], not_7_out);
  and and_5 (S3, not_8_out, A_B_C[1], A_B_C[0]);
  and and_6 (S4, A_B_C[2], not_9_out, not_10_out);
  and and_7 (S5, A_B_C[2], not_11_out, A_B_C[0]);
  and and_8 (S6, A_B_C[2], A_B_C[1], not_12_out);
endmodule

module OR_4 (
  input  [3:0] in_1,
  input  [3:0] in_2,
  output [3:0] out_3
);

  or or_1 (out_3[0], in_1[0], in_2[0]);
  or or_2 (out_3[1], in_1[1], in_2[1]);
  or or_3 (out_3[2], in_1[2], in_2[2]);
  or or_4 (out_3[3], in_1[3], in_2[3]);
endmodule

module Rot_L (
  input  [3:0] ABCD,
  input  [1:0] XY,
  output [3:0] abcd_2
);

  wire and_1_out, and_2_out, and_3_out, and_4_out, and_5_out, and_6_out, and_7_out, and_8_out, and_9_out;

  and and_1 (and_1_out, ~XY[1], ~XY[0], ABCD[3]);  // AND_Gate
  and and_2 (and_2_out, ~XY[1], XY[0], ABCD[2]);  // AND_Gate
  and and_3 (and_3_out, XY[1], ~XY[0], ABCD[1]);  // AND_Gate
  and and_4 (and_4_out, XY[1], XY[0], ABCD[0]);
  and and_5 (and_5_out, ~XY[1], ~XY[0], ABCD[2]);  // AND_Gate
  and and_6 (and_6_out, ~XY[1], XY[0], ABCD[1]);  // AND_Gate
  and and_7 (and_7_out, XY[1], ~XY[0], ABCD[0]);  // AND_Gate
  and and_8 (and_8_out, ~XY[1], ~XY[0], ABCD[1]);  // AND_Gate
  and and_9 (and_9_out, ~XY[1], XY[0], ABCD[0]);  // AND_Gate
  and and_10 (abcd_2[0], ~XY[1], ~XY[0], ABCD[0]);  // AND_Gate
  or or_1 (abcd_2[3], and_1_out, and_2_out, and_3_out, and_4_out);
  or or_2 (abcd_2[2], and_5_out, and_6_out, and_7_out);
  or or_3 (abcd_2[1], and_8_out, and_9_out);

  // Notes on the sheet:
  //   a 🐞
  //   b🐶
  //   c🦎
  //   d🐽
endmodule

module Rot_R (
  input  [3:0] ABCD,
  input  [1:0] XY,
  output [3:0] abcd_2
);

  wire and_1_out, and_2_out, and_3_out, and_4_out, and_5_out, and_6_out, and_7_out, and_8_out, and_9_out;

  and and_1 (and_1_out, ~XY[1], ~XY[0], ABCD[0]);  // AND_Gate
  and and_2 (and_2_out, ~XY[1], XY[0], ABCD[1]);  // AND_Gate
  and and_3 (and_3_out, XY[1], ~XY[0], ABCD[2]);  // AND_Gate
  and and_4 (and_4_out, XY[1], XY[0], ABCD[3]);
  and and_5 (and_5_out, ~XY[1], ~XY[0], ABCD[1]);  // AND_Gate
  and and_6 (and_6_out, ~XY[1], XY[0], ABCD[2]);  // AND_Gate
  and and_7 (and_7_out, XY[1], ~XY[0], ABCD[3]);  // AND_Gate
  and and_8 (and_8_out, ~XY[1], ~XY[0], ABCD[2]);  // AND_Gate
  and and_9 (and_9_out, ~XY[1], XY[0], ABCD[3]);  // AND_Gate
  and and_10 (abcd_2[3], ~XY[1], ~XY[0], ABCD[3]);  // AND_Gate
  or or_1 (abcd_2[0], and_1_out, and_2_out, and_3_out, and_4_out);
  or or_2 (abcd_2[1], and_5_out, and_6_out, and_7_out);
  or or_3 (abcd_2[2], and_8_out, and_9_out);

  // Notes on the sheet:
  //   a 🐞
  //   b🐶
  //   c🦎
  //   d🐽
endmodule

module ALU (
  input  \Direção ,
  input  [3:0] A,
  input  [3:0] B,
  input  [2:0] \Operações ,
  output Overflow,
  output [3:0] Saida,
  output Zero
);

  wire add_4_1_vem_1, and_1_out, and_2_out, decoder_1_s0, decoder_1_s1, decoder_1_s2, decoder_1_s3,
       decoder_1_s4, decoder_1_s5, decoder_1_s6, decoder_1_s7, not_1_out, sub_4_1_overflow;
  wire [3:0] add_4_1_out_5, buffer_5_saida, or_4_1_out_3, rot_l_1_abcd_2, rot_r_1_abcd_2, sub_4_1_out_5;

  and and_1 (and_1_out, add_4_1_vem_1, decoder_1_s1);
  or or_1 (Overflow, and_1_out, and_2_out);
  and and_2 (and_2_out, sub_4_1_overflow, decoder_1_s2);
  Decoder decoder_1 (
    .A_B_C(\Operações ), .S0(decoder_1_s0), .S1(decoder_1_s1), .S2(decoder_1_s2), .S3(decoder_1_s3),
    .S4(decoder_1_s4), .S5(decoder_1_s5), .S6(decoder_1_s6), .S7(decoder_1_s7));
  // Probe on A
  // Probe on B
  Buffer buffer_1 (.B(B), .in_2(decoder_1_s0), .Saida(Saida));
  nor nor_1 (Zero, decoder_1_s7, decoder_1_s6, Saida[3], Saida[0], Saida[1], Saida[2]);
  Add_4 add_4_1 (.in_2(A), .Vem_1(add_4_1_vem_1), .in_1(B), .Vem__1(1'b0), .out_5(add_4_1_out_5));
  Buffer buffer_2 (.B(add_4_1_out_5), .in_2(decoder_1_s1), .Saida(Saida));
  Sub_4 sub_4_1 (.A(A), .Overflow(sub_4_1_overflow), .B(B), .Vem_1(1'b0), .out_5(sub_4_1_out_5));
  Buffer buffer_3 (.B(sub_4_1_out_5), .in_2(decoder_1_s2), .Saida(Saida));
  // Probe on Saida
  OR_4 or_4_1 (.in_1(A), .in_2(B), .out_3(or_4_1_out_3));
  Buffer buffer_4 (.B(or_4_1_out_3), .in_2(decoder_1_s3), .Saida(Saida));
  Buffer_N buffer_n_1 (.B(B), .in_2(decoder_1_s4), .Saida(Saida));
  Buffer buffer_5 (.B(rot_r_1_abcd_2), .in_2(\Direção ), .Saida(buffer_5_saida));
  Rot_R rot_r_1 (.abcd_2(rot_r_1_abcd_2), .ABCD(A), .XY(B[1:0]));
  Rot_L rot_l_1 (.abcd_2(rot_l_1_abcd_2), .ABCD(A), .XY(B[1:0]));
  Buffer buffer_6 (.B(rot_l_1_abcd_2), .in_2(not_1_out), .Saida(buffer_5_saida));
  not not_1 (not_1_out, \Direção );
  Buffer buffer_7 (.B(buffer_5_saida), .in_2(decoder_1_s5), .Saida(Saida));
endmodule

module AC (
  input  Clock,
  input  [3:0] D,
  output [3:0] Q
);

  D_Flip_Flop d_ff_1 (.clk(Clock), .D(D[3]), .Q(Q[3]));  // open: Qn, preset, en, reset
  D_Flip_Flop d_ff_2 (.clk(Clock), .D(D[2]), .Q(Q[2]));  // open: Qn, preset, en, reset
  D_Flip_Flop d_ff_3 (.clk(Clock), .D(D[1]), .Q(Q[1]));  // open: Qn, preset, en, reset
  D_Flip_Flop d_ff_4 (.clk(Clock), .D(D[0]), .Q(Q[0]));  // open: Qn, preset, en, reset
endmodule

module Mux (
  input  [3:0] E,
  input  [3:0] D,
  input  Controle,
  output [3:0] S
);

  wire not_1_out;

  not not_1 (not_1_out, Controle);
  Buffer buffer_1 (.B(E), .in_2(not_1_out), .Saida(S));
  Buffer buffer_2 (.B(D), .in_2(Controle), .Saida(S));
endmodule

module IR (
  input  Clock,
  input  [7:0] D,
  output [7:0] Q
);

  D_Flip_Flop #(.trigger("falling")) d_ff_1 (.clk(Clock), .D(D[7]), .Q(Q[7]));  // open: Qn, preset, en, reset
  D_Flip_Flop #(.trigger("falling")) d_ff_2 (.clk(Clock), .D(D[6]), .Q(Q[6]));  // open: Qn, preset, en, reset
  D_Flip_Flop #(.trigger("falling")) d_ff_3 (.clk(Clock), .D(D[5]), .Q(Q[5]));  // open: Qn, preset, en, reset
  D_Flip_Flop #(.trigger("falling")) d_ff_4 (.clk(Clock), .D(D[4]), .Q(Q[4]));  // open: Qn, preset, en, reset
  D_Flip_Flop #(.trigger("falling")) d_ff_5 (.clk(Clock), .D(D[3]), .Q(Q[3]));  // open: Qn, preset, en, reset
  D_Flip_Flop #(.trigger("falling")) d_ff_6 (.clk(Clock), .D(D[2]), .Q(Q[2]));  // open: Qn, preset, en, reset
  D_Flip_Flop #(.trigger("falling")) d_ff_7 (.clk(Clock), .D(D[1]), .Q(Q[1]));  // open: Qn, preset, en, reset
  D_Flip_Flop #(.trigger("falling")) d_ff_8 (.clk(Clock), .D(D[0]), .Q(Q[0]));  // open: Qn, preset, en, reset
endmodule

module Unidade_de_Controle (
  input  [7:0] \Instrução ,
  input  Clock,
  input  Reset,
  input  Zero,
  input  OverFlow,
  output [3:0] Dados,
  output [3:0] \B_Endereços ,
  output clk_Rl,
  output clk_AG,
  output clk_Ram,
  output [3:0] Operando,
  output Rst_Pc,
  output \Direção ,
  output clk_PC,
  output E,
  output [2:0] \Operação ,
  output r_w,
  output Load
);

  wire and_1_out, and_4_out, and_7_out, nand_2_out;
  wire [1:0] counter_1_q;

  nand nand_1 (r_w, \Instrução [7], \Instrução [6], \Instrução [5], \Instrução [4], clk_AG);
  Counter #(.width(2), .max('h3)) counter_1 (.Q(counter_1_q), .clk(Clock), .clr(Reset));  // open: load, D, count, carry
  and and_1 (and_1_out, \Instrução [7], \Instrução [6], \Instrução [5], ~\Instrução [4], clk_PC);  // AND_Gate
  and and_2 (clk_Rl, ~counter_1_q[0], ~counter_1_q[1]);  // AND_Gate
  and and_3 (clk_PC, counter_1_q[0], ~counter_1_q[1]);  // AND_Gate
  and and_4 (and_4_out, \Instrução [7], \Instrução [6], ~\Instrução [5], \Instrução [4], clk_PC, OverFlow);  // AND_Gate
  or or_1 (Load, and_1_out, and_4_out, and_7_out);
  and and_5 (clk_Ram, counter_1_q[0], counter_1_q[1]);
  and and_6 (clk_AG, ~counter_1_q[0], counter_1_q[1]);  // AND_Gate
  and and_7 (and_7_out, \Instrução [7], \Instrução [6], ~\Instrução [5], ~\Instrução [4], clk_PC, Zero);  // AND_Gate
  nand nand_2 (nand_2_out, \Instrução [7], ~\Instrução [6], \Instrução [5]);  // NAND_Gate
  and and_8 (E, \Instrução [4], nand_2_out);

  assign \B_Endereços  = \Instrução [3:0];
  assign Dados = \Instrução [3:0];
  assign \Direção  = \Instrução [4];
  assign Operando = \Instrução [3:0];
  assign \Operação  = \Instrução [7:5];
  assign Rst_Pc = Reset;
endmodule
